// Logisim project tf_arqui.circ as structural Verilog: 3 circuits, main circuit CPU
module CPU (
);

  wire clock_1_out, reset;
  wire [7:0] adder_1_out, PC_q, rom_1_data;

  Clock clock_1 (.out(clock_1_out));
  Register PC (.D(adder_1_out), .en(1'b1), .clk(clock_1_out), .Q(PC_q), .clr(reset));
  Adder adder_1 (.a(8'h1), .b(PC_q), .out(adder_1_out));  // open: cin, cout
  ROM rom_1 (.addr(PC_q), .data(rom_1_data));
  bancoRegistrador bancoregistrador_1 ();  // open: RegValue, RegA, RegB, Reset, RegWrite, SaidaA, SaidaB
endmodule

module bancoRegistrador (
  input  [7:0] RegValue,
  input  [1:0] RegA,
  input  [1:0] RegB,
  input  Reset,
  output [7:0] SaidaA,
  output [7:0] SaidaB,
  output RegWrite
);

  wire clock_1_out, demultiplexer_1_out0, demultiplexer_1_out1, demultiplexer_1_out2, demultiplexer_1_out3;
  wire [7:0] r0_q, r1_q, r2_q, r3_q;

  Demultiplexer #(.select(2)) demultiplexer_1 (
    .out0(demultiplexer_1_out0), .out1(demultiplexer_1_out1), .out2(demultiplexer_1_out2),
    .out3(demultiplexer_1_out3), .in(RegWrite), .sel(RegA));
  Register r0 (.D(RegValue), .en(demultiplexer_1_out0), .clk(clock_1_out), .Q(r0_q), .clr(Reset));
  Register r1 (.D(RegValue), .en(demultiplexer_1_out1), .clk(clock_1_out), .Q(r1_q), .clr(Reset));
  Clock clock_1 (.out(clock_1_out));
  Register r2 (.D(RegValue), .en(demultiplexer_1_out2), .clk(clock_1_out), .Q(r2_q), .clr(Reset));
  Register r3 (.D(RegValue), .en(demultiplexer_1_out3), .clk(clock_1_out), .Q(r3_q), .clr(Reset));
  Multiplexer #(.select(2), .width(8)) multiplexer_1 (
    .in0(r0_q), .in1(r1_q), .in2(r2_q), .in3(r3_q), .out(SaidaA), .sel(RegA));
  Multiplexer #(.select(2), .width(8)) multiplexer_2 (
    .in0(r0_q), .in1(r1_q), .in2(r2_q), .in3(r3_q), .out(SaidaB), .sel(RegB));

  // Notes on the sheet:
  //   r0
  //   r2
endmodule

module Ula (
  input  [3:0] A,
  input  [3:0] B,
  input  [2:0] OpULA,
  output zero,
  output [3:0] saida
);

  wire [3:0] adder_1_out, and_1_out, divider_1_out, multiplier_1_out, not_1_out, or_1_out, subtractor_1_out;

  assign not_1_out = ~B;  // NOT_Gate not_1, 4 bits wide
  Adder #(.width(4)) adder_1 (.a(A), .b(B), .out(adder_1_out));  // open: cin, cout
  Subtractor #(.width(4)) subtractor_1 (.a(A), .b(B), .out(subtractor_1_out));  // open: bin, bout
  assign and_1_out = A & B;  // AND_Gate and_1, 4 bits wide
  assign or_1_out = A | B;  // OR_Gate or_1, 4 bits wide
  Multiplier #(.width(4)) multiplier_1 (.a(B), .b(4'b0010), .out(multiplier_1_out));  // open: cin, cout
  Divider #(.width(4)) divider_1 (.a(B), .b(4'b0010), .out(divider_1_out));  // open: upper, rem
  Multiplexer #(.select(3), .width(4)) multiplexer_1 (
    .in0(adder_1_out), .in1(subtractor_1_out), .in2(and_1_out), .in3(or_1_out), .in4(not_1_out),
    .in5(multiplier_1_out), .in6(divider_1_out), .out(saida), .sel(OpULA));  // open: in7
  Comparator #(.width(4)) comparator_1 (.a(4'b0000), .b(saida), .eq(zero));  // open: gt, lt
endmodule
